# Fritzing sketch robobatteur (saved by Fritzing 0.9.9b)
stripboards: 1
breadboards: 1

parts:
  Power_plug1 = Power plug
  Composant1 = Arduino Uno (Rev3)
  U2 = OPTO_DARL_6N138S [package=8-smd]
  R4 = Resistor [tolerance=±5% power=0.25 resistance=220 package=THT]
  DIN2 = DIN-5 jack (MIDI) [package=THT]
  R6 = Resistor [tolerance=±5% power=0.25 resistance=220 package=THT]
  D2 = Rectifier Diode [part_number=1N4001 package="300 mil [THT]"]
  R7 = Resistor [tolerance=±5% power=0.25 resistance=4.7k package=THT]
  C1 = Electrolytic Capacitor [capacitance=100µF voltage=35V package="100 mil [THT, electrolytic]"]
  J2 = Basic Servo [part_number=MG996R]
  Power_plug2 = Power plug
  C2 = Electrolytic Capacitor [capacitance=47µF voltage=35V package="100 mil [THT, electrolytic]"]
  C3 = Electrolytic Capacitor [capacitance=47µF voltage=35V package="100 mil [THT, electrolytic]"]
  Power_plug3 = Power plug
  J1 = Basic Servo [part_number=MG996R]
  J3 = Basic Servo [part_number=MG996R]
  J4 = Basic Servo [part_number=MG996R]
  J5 = Basic Servo [part_number=MG996R]
  J6 = Basic Servo [part_number=MG996R]
  J7 = Basic Servo [part_number=MG996R]
  J8 = Basic Servo [part_number=MG996R]
  Power_plug4 = Power plug
  C4 = Electrolytic Capacitor [capacitance=47µF voltage=35V package="100 mil [THT, electrolytic]"]

nets:
  GND: Power_plug1.GND, Composant1.GND, U2.GND, R7.Pin_1, C1.-, J2.gnd, Power_plug2.GND, C2.-, C3.-, Power_plug3.GND, J1.gnd, J3.gnd, J4.gnd, J5.gnd, J6.gnd, J7.gnd, J8.gnd, Power_plug4.GND, C4.-
  VCC: Power_plug1.VCC, C1.+, J2.vcc, J1.vcc
  N1: Composant1.D8, J6.pulse
  N2: Composant1.D9_PWM, J5.pulse
  N3: Composant1.D10_PWM/SS, J2.pulse
  N4: Composant1.D11_PWM/MOSI, J1.pulse
  N5: Composant1.D0/RX, U2.VOUT, R4.Pin_1
  N6: Composant1.D4, J3.pulse
  N7: Composant1.D5_PWM, J4.pulse
  N8: Composant1.D6_PWM, J8.pulse
  N9: Composant1.D7, J7.pulse
  5V: Composant1.5V, U2.VCC, R4.Pin_0
  N10: U2.A, DIN2.5, R6.Pin_0, D2.cathode
  N11: U2.C, D2.anode
  N12: DIN2.4, R6.Pin_1
  VCC_2: Power_plug2.VCC, C2.+, J5.vcc, J6.vcc
  VCC_3: C3.+, Power_plug3.VCC, J7.vcc, J8.vcc
  VCC_4: J3.vcc, J4.vcc, Power_plug4.VCC, C4.+
